# Fritzing sketch Capstone Draw (saved by Fritzing 0.9.3b)

parts:
  SIM_800A = SIM800L [package=THT]
  RELAY = RELAY [package=relay-jzc]
  DC_in = Power Jack [package=power_jack_smd]
  DS1307 = Real Time Clock Module - DS1307 RTC Breakout Board
  AC = AC Power [voltage=220 frequency=60]
  PUMP = DC Motor
  AC_To_DC = ADMP504 - Ultralow Noise Microphone with Bottom Port and Analog Output [part_number=ADMP504]
  Part3 = Arduino Mega 2560 (Rev3)

nets:
  GND: SIM_800A.GND#1, RELAY.COIL2, DS1307.GND, AC_To_DC.OUTPUT, Part3.GND
  VDD: SIM_800A.VDD, DC_in.GNDBREAK, Part3.VIN
  N1: SIM_800A.SIM_TXD, Part3.D50
  N2: SIM_800A.SIM_RXD, Part3.D51
  N3: SIM_800A.GND#5, DC_in.GND
  N4: RELAY.NC, PUMP.pin_1, AC_To_DC.NC
  N5: RELAY.MAIN, AC.V-
  N6: RELAY.COIL1, Part3.D12_PWM
  5V: DS1307.5V, Part3.5V
  N7: DS1307.SCL, Part3.D21/SCL
  N8: DS1307.SDA, Part3.D20/SDA
  N9: AC.V+, PUMP.pin_2
  N10: AC_To_DC.GND, Part3.D11_PWM
